// Logisim project NetworkArchitecture.circ as structural Verilog
module main (
);

  wire A_0Write, A_1Write, A_2Write, A_3Write, A_4Write, A_5Write, A_6Write, A_7Write, B_0Write, B_1Write,
       CLEAR;
  wire [2:0] W_SLCT;
  wire [7:0] A_0E0, A_0E1, A_0E2, A_0E3, A_0E4, A_0E5, A_0E6, A_0E7, A_1E0, A_1E2, A_1E3, A_1E4, A_1E5,
       A_1E6, A_1E7, A_2E0, A_2E1, A_2E2, A_2E3, A_2E4, A_2E5, A_2E6, A_2E7, A_3E0, A_3E1, A_3E2, A_3E3,
       A_3E4, A_3E5, A_3E6, A_3E7, A_4E0, A_4E1, A_4E2, A_4E3, A_4E4, A_4E5, A_4E6, A_4E7, A_5E0, A_5E1,
       A_5E2, A_5E3, A_5E4, A_5E5, A_5E6, A_5E7, A_6E0, A_6E1, A_6E2, A_6E3, A_6E4, A_6E5, A_6E6, A_6E7,
       A_7E0, A_7E1, A_7E2, A_7E3, A_7E4, A_7E5, A_7E6, A_7E7, B_0E0, B_0E1, B_0E2, B_0E3, B_0E4, B_0E5,
       B_0E6, B_0E7, B_1E0, B_1E1, B_1E2, B_1E3, B_1E4, B_1E5, B_1E6, B_1E7, WGHT_IN;

  LinearNode linearnode_1 (
    .E0(A_0E0), .E1(A_0E1), .E2(A_0E2), .E3(A_0E3), .E4(A_0E4), .E5(A_0E5), .E6(A_0E6), .E7(A_0E7),
    .W_WRITE(A_0Write), .W_SLCT(W_SLCT), .W_IN(WGHT_IN), .CLEAR(CLEAR));  // open: IN_0, IN_1, IN_2, IN_3, IN_4, IN_5, IN_6, IN_7, CLK
  LinearNode linearnode_2 (
    .E0(A_1E0), .E1(A_0E1), .E2(A_1E2), .E3(A_1E3), .E4(A_1E4), .E5(A_1E5), .E6(A_1E6), .E7(A_1E7),
    .W_WRITE(A_1Write), .W_SLCT(W_SLCT), .W_IN(WGHT_IN), .CLEAR(CLEAR));  // open: IN_0, IN_1, IN_2, IN_3, IN_4, IN_5, IN_6, IN_7, CLK
  LinearNode linearnode_3 (
    .E0(A_2E0), .E1(A_2E1), .E2(A_2E2), .E3(A_2E3), .E4(A_2E4), .E5(A_2E5), .E6(A_2E6), .E7(A_2E7),
    .W_WRITE(A_2Write), .W_SLCT(W_SLCT), .W_IN(WGHT_IN), .CLEAR(CLEAR));  // open: IN_0, IN_1, IN_2, IN_3, IN_4, IN_5, IN_6, IN_7, CLK
  LinearNode linearnode_4 (
    .E0(A_3E0), .E1(A_3E1), .E2(A_3E2), .E3(A_3E3), .E4(A_3E4), .E5(A_3E5), .E6(A_3E6), .E7(A_3E7),
    .W_WRITE(A_3Write), .W_SLCT(W_SLCT), .W_IN(WGHT_IN), .CLEAR(CLEAR));  // open: IN_0, IN_1, IN_2, IN_3, IN_4, IN_5, IN_6, IN_7, CLK
  LinearNode linearnode_5 (
    .E0(A_4E0), .E1(A_4E1), .E2(A_4E2), .E3(A_4E3), .E4(A_4E4), .E5(A_4E5), .E6(A_4E6), .E7(A_4E7),
    .W_WRITE(A_4Write), .W_SLCT(W_SLCT), .W_IN(WGHT_IN), .CLEAR(CLEAR));  // open: IN_0, IN_1, IN_2, IN_3, IN_4, IN_5, IN_6, IN_7, CLK
  LinearNode linearnode_6 (
    .E0(A_5E0), .E1(A_5E1), .E2(A_5E2), .E3(A_5E3), .E4(A_5E4), .E5(A_5E5), .E6(A_5E6), .E7(A_5E7),
    .W_WRITE(A_5Write), .W_SLCT(W_SLCT), .W_IN(WGHT_IN), .CLEAR(CLEAR));  // open: IN_0, IN_1, IN_2, IN_3, IN_4, IN_5, IN_6, IN_7, CLK
  LinearNode linearnode_7 (
    .E0(A_6E0), .E1(A_6E1), .E2(A_6E2), .E3(A_6E3), .E4(A_6E4), .E5(A_6E5), .E6(A_6E6), .E7(A_6E7),
    .W_WRITE(A_6Write), .W_SLCT(W_SLCT), .W_IN(WGHT_IN), .CLEAR(CLEAR));  // open: IN_0, IN_1, IN_2, IN_3, IN_4, IN_5, IN_6, IN_7, CLK
  LinearNode linearnode_8 (
    .E0(A_7E0), .E1(A_7E1), .E2(A_7E2), .E3(A_7E3), .E4(A_7E4), .E5(A_7E5), .E6(A_7E6), .E7(A_7E7),
    .W_WRITE(A_7Write), .W_SLCT(W_SLCT), .W_IN(WGHT_IN), .CLEAR(CLEAR));  // open: IN_0, IN_1, IN_2, IN_3, IN_4, IN_5, IN_6, IN_7, CLK
  LinearNode linearnode_9 (
    .IN_0(A_0E0), .IN_1(A_1E0), .IN_2(A_2E0), .IN_3(A_3E0), .IN_4(A_4E0), .IN_5(A_5E0), .IN_6(A_6E0),
    .IN_7(A_7E0), .E0(B_0E0), .E1(B_0E1), .E2(B_0E2), .E3(B_0E3), .E4(B_0E4), .E5(B_0E5), .E6(B_0E6),
    .E7(B_0E7), .W_WRITE(B_0Write), .W_SLCT(W_SLCT), .W_IN(WGHT_IN), .CLEAR(CLEAR));  // open: CLK
  LinearNode linearnode_10 (
    .IN_0(A_0E1), .IN_1(A_0E1), .IN_2(A_2E1), .IN_3(A_3E1), .IN_4(A_4E1), .IN_5(A_5E1), .IN_6(A_6E1),
    .IN_7(A_7E1), .E0(B_1E0), .E1(B_1E1), .E2(B_1E2), .E3(B_1E3), .E4(B_1E4), .E5(B_1E5), .E6(B_1E6),
    .E7(B_1E7), .W_WRITE(B_1Write), .W_SLCT(W_SLCT), .W_IN(WGHT_IN), .CLEAR(CLEAR));  // open: CLK
  LinearNode linearnode_11 (
    .IN_0(A_0E2), .IN_1(A_1E2), .IN_2(A_2E2), .IN_3(A_3E2), .IN_4(A_4E2), .IN_5(A_5E2), .IN_6(A_6E2),
    .IN_7(A_7E2), .E0(A_2E0), .E1(A_2E1), .E2(A_2E2), .E3(A_2E3), .E4(A_2E4), .E5(A_2E5), .E6(A_2E6),
    .E7(A_2E7), .W_WRITE(A_2Write), .W_SLCT(W_SLCT), .W_IN(WGHT_IN), .CLEAR(CLEAR));  // open: CLK
  LinearNode linearnode_12 (
    .IN_0(A_0E3), .IN_1(A_1E3), .IN_2(A_2E3), .IN_3(A_3E3), .IN_4(A_4E3), .IN_5(A_5E3), .IN_6(A_6E3),
    .IN_7(A_7E3), .E0(A_3E0), .E1(A_3E1), .E2(A_3E2), .E3(A_3E3), .E4(A_3E4), .E5(A_3E5), .E6(A_3E6),
    .E7(A_3E7), .W_WRITE(A_3Write), .W_SLCT(W_SLCT), .W_IN(WGHT_IN), .CLEAR(CLEAR));  // open: CLK
  LinearNode linearnode_13 (
    .IN_0(A_0E4), .IN_1(A_1E4), .IN_2(A_2E4), .IN_3(A_3E4), .IN_4(A_4E4), .IN_5(A_5E4), .IN_6(A_6E4),
    .IN_7(A_7E4), .E0(A_4E0), .E1(A_4E1), .E2(A_4E2), .E3(A_4E3), .E4(A_4E4), .E5(A_4E5), .E6(A_4E6),
    .E7(A_4E7), .W_WRITE(A_4Write), .W_SLCT(W_SLCT), .W_IN(WGHT_IN), .CLEAR(CLEAR));  // open: CLK
  LinearNode linearnode_14 (
    .IN_0(A_0E5), .IN_1(A_1E5), .IN_2(A_2E5), .IN_3(A_3E5), .IN_4(A_4E5), .IN_5(A_5E5), .IN_6(A_6E5),
    .IN_7(A_7E5), .E0(A_5E0), .E1(A_5E1), .E2(A_5E2), .E3(A_5E3), .E4(A_5E4), .E5(A_5E5), .E6(A_5E6),
    .E7(A_5E7), .W_WRITE(A_5Write), .W_SLCT(W_SLCT), .W_IN(WGHT_IN), .CLEAR(CLEAR));  // open: CLK
  LinearNode linearnode_15 (
    .IN_0(A_0E6), .IN_1(A_1E6), .IN_2(A_2E6), .IN_3(A_3E6), .IN_4(A_4E6), .IN_5(A_5E6), .IN_6(A_6E6),
    .IN_7(A_7E6), .E0(A_6E0), .E1(A_6E1), .E2(A_6E2), .E3(A_6E3), .E4(A_6E4), .E5(A_6E5), .E6(A_6E6),
    .E7(A_6E7), .W_WRITE(A_6Write), .W_SLCT(W_SLCT), .W_IN(WGHT_IN), .CLEAR(CLEAR));  // open: CLK
  LinearNode linearnode_16 (
    .IN_0(A_0E7), .IN_1(A_1E7), .IN_2(A_2E7), .IN_3(A_3E7), .IN_4(A_4E7), .IN_5(A_5E7), .IN_6(A_6E7),
    .IN_7(A_7E7), .E0(A_7E0), .E1(A_7E1), .E2(A_7E2), .E3(A_7E3), .E4(A_7E4), .E5(A_7E5), .E6(A_7E6),
    .E7(A_7E7), .W_WRITE(A_7Write), .W_SLCT(W_SLCT), .W_IN(WGHT_IN), .CLEAR(CLEAR));  // open: CLK

  // Other names for the same wires on the sheet: A_1E1[7:0] = A_0E1
endmodule

module LinearNode (
  input  [7:0] IN_0,
  input  [7:0] E0,
  input  [7:0] IN_1,
  input  [7:0] E1,
  input  [7:0] IN_2,
  input  [7:0] E2,
  input  [7:0] IN_3,
  input  [7:0] E3,
  input  [7:0] IN_4,
  input  [7:0] E4,
  input  [7:0] IN_5,
  input  [7:0] E5,
  input  [7:0] IN_6,
  input  [7:0] E6,
  input  [7:0] IN_7,
  input  [7:0] E7,
  input  W_WRITE,
  input  [2:0] W_SLCT,
  input  [7:0] W_IN,
  input  CLEAR,
  input  CLK
);

  wire decoder_1_out0, decoder_1_out1, decoder_1_out2, decoder_1_out3, decoder_1_out4, decoder_1_out5,
       decoder_1_out6, decoder_1_out7, W0_Write, W1_Write, W2_Write, W3_Write, W4_Write, W5_Write, W6_Write,
       W7_Write;
  wire [7:0] adder_1_out, adder_2_out, adder_3_out, adder_4_out, adder_5_out, adder_6_out, adder_7_out, BIAS,
       FUNC_OUT, multiplier_1_out, multiplier_2_out, multiplier_3_out, multiplier_4_out, multiplier_5_out,
       multiplier_6_out, multiplier_7_out, multiplier_8_out, W0, W1, W2, W3, W4, W5, W6, W7;

  Decoder #(.select(3), .disabled(0), .enable("false")) decoder_1 (
    .out0(decoder_1_out0), .out1(decoder_1_out1), .out2(decoder_1_out2), .out3(decoder_1_out3),
    .out4(decoder_1_out4), .out5(decoder_1_out5), .out6(decoder_1_out6), .out7(decoder_1_out7), .sel(W_SLCT));
  Adder adder_1 (.a(IN_0), .b(IN_1), .out(adder_1_out), .cin(1'b0));  // open: cout
  Adder adder_2 (.a(IN_2), .b(IN_3), .out(adder_2_out), .cin(1'b0));  // open: cout
  Adder adder_3 (.a(IN_4), .b(IN_5), .out(adder_3_out), .cin(1'b0));  // open: cout
  Adder adder_4 (.a(IN_6), .b(IN_7), .out(adder_4_out), .cin(1'b0));  // open: cout
  and and_1 (W0_Write, decoder_1_out0, W_WRITE);
  and and_2 (W1_Write, decoder_1_out1, W_WRITE);
  and and_3 (W2_Write, decoder_1_out2, W_WRITE);
  and and_4 (W3_Write, decoder_1_out3, W_WRITE);
  and and_5 (W4_Write, decoder_1_out4, W_WRITE);
  and and_6 (W5_Write, decoder_1_out5, W_WRITE);
  and and_7 (W6_Write, decoder_1_out6, W_WRITE);
  and and_8 (W7_Write, decoder_1_out7, W_WRITE);
  Adder adder_5 (.a(adder_1_out), .b(adder_2_out), .out(adder_5_out), .cin(1'b0));  // open: cout
  Adder adder_6 (.a(adder_3_out), .b(adder_4_out), .out(adder_6_out), .cin(1'b0));  // open: cout
  Adder adder_7 (.a(adder_5_out), .b(adder_6_out), .out(adder_7_out), .cin(1'b0));  // open: cout
  Adder adder_8 (.a(adder_7_out), .b(BIAS), .out(FUNC_OUT), .cin(1'b0));  // open: cout
  Register #(.trigger("high")) register_1 (.D(W_IN), .en(1'b1), .Q(W0), .clk(W0_Write), .clr(CLEAR));
  Register #(.trigger("high")) register_2 (.D(W_IN), .en(1'b1), .Q(W1), .clk(W1_Write), .clr(CLEAR));
  Register #(.trigger("high")) register_3 (.D(W_IN), .en(1'b1), .Q(W2), .clk(W2_Write), .clr(CLEAR));
  Register #(.trigger("high")) register_4 (.D(W_IN), .en(1'b1), .Q(W3), .clk(W3_Write), .clr(CLEAR));
  Register #(.trigger("high")) register_5 (.D(W_IN), .en(1'b1), .Q(W4), .clk(W4_Write), .clr(CLEAR));
  Register #(.trigger("high")) register_6 (.D(W_IN), .en(1'b1), .Q(W5), .clk(W5_Write), .clr(CLEAR));
  Register #(.trigger("high")) register_7 (.D(W_IN), .en(1'b1), .Q(W6), .clk(W6_Write), .clr(CLEAR));
  Register #(.trigger("high")) register_8 (.D(W_IN), .en(1'b1), .Q(W7), .clk(W7_Write), .clr(CLEAR));
  Multiplier multiplier_1 (.a(FUNC_OUT), .b(W0), .out(multiplier_1_out), .cin({8{1'b0}}));  // open: cout
  Multiplier multiplier_2 (.a(FUNC_OUT), .b(W1), .out(multiplier_2_out), .cin({8{1'b0}}));  // open: cout
  Multiplier multiplier_3 (.a(FUNC_OUT), .b(W2), .out(multiplier_3_out), .cin({8{1'b0}}));  // open: cout
  Multiplier multiplier_4 (.a(FUNC_OUT), .b(W3), .out(multiplier_4_out), .cin({8{1'b0}}));  // open: cout
  Multiplier multiplier_5 (.a(FUNC_OUT), .b(W4), .out(multiplier_5_out), .cin({8{1'b0}}));  // open: cout
  Multiplier multiplier_6 (.a(FUNC_OUT), .b(W5), .out(multiplier_6_out), .cin({8{1'b0}}));  // open: cout
  Multiplier multiplier_7 (.a(FUNC_OUT), .b(W6), .out(multiplier_7_out), .cin({8{1'b0}}));  // open: cout
  Multiplier multiplier_8 (.a(FUNC_OUT), .b(W7), .out(multiplier_8_out), .cin({8{1'b0}}));  // open: cout
  Register #(.trigger("high")) register_9 (.D(multiplier_1_out), .en(1'b1), .Q(E0), .clk(CLK), .clr(CLEAR));
  Register #(.trigger("high")) register_10 (.D(multiplier_2_out), .en(1'b1), .Q(E1), .clk(CLK), .clr(CLEAR));
  Register #(.trigger("high")) register_11 (.D(multiplier_3_out), .en(1'b1), .Q(E2), .clk(CLK), .clr(CLEAR));
  Register #(.trigger("high")) register_12 (.D(multiplier_4_out), .en(1'b1), .Q(E3), .clk(CLK), .clr(CLEAR));
  Register #(.trigger("high")) register_13 (.D(multiplier_5_out), .en(1'b1), .Q(E4), .clk(CLK), .clr(CLEAR));
  Register #(.trigger("high")) register_14 (.D(multiplier_6_out), .en(1'b1), .Q(E5), .clk(CLK), .clr(CLEAR));
  Register #(.trigger("high")) register_15 (.D(multiplier_7_out), .en(1'b1), .Q(E6), .clk(CLK), .clr(CLEAR));
  Register #(.trigger("high")) register_16 (.D(multiplier_8_out), .en(1'b1), .Q(E7), .clk(CLK), .clr(CLEAR));

  // Other names for the same wires on the sheet: E0_OUT[7:0] = E0; E1_OUT[7:0] = E1; E2_OUT[7:0] = E2;
  //   E3_OUT[7:0] = E3; E4_OUT[7:0] = E4; E5_OUT[7:0] = E5; E6_OUT[7:0] = E6; E7_OUT[7:0] = E7;
  //   W_SELECT[2:0] = W_SLCT

  // Notes on the sheet:
  //   Linear Addition
  //   Weight Writing/Storage
  //   Weight Multiplication
  //   Input
  //   Output
endmodule

module LinearNode_Bus (
  input  [7:0] IN,
  input  FUNC_CLEAR,
  input  EVALUATE,
  input  W_WRITE,
  input  [2:0] W_SLCT,
  input  [7:0] W_IN,
  input  CLEAR,
  input  CLK,
  output [7:0] E0,
  output [7:0] E1,
  output [7:0] E2,
  output [7:0] E3,
  output [7:0] E4,
  output [7:0] E5,
  output [7:0] E6,
  output [7:0] E7
);

  wire not_1_out;
  wire [7:0] adder_1_out, BIAS, FUNC_OUT, multiplier_1_out, multiplier_2_out, multiplier_3_out,
       multiplier_4_out, multiplier_5_out, multiplier_6_out, multiplier_7_out, multiplier_8_out,
       register_1_q, transmission_1_p4, W0, W1, W2, W3, W4, W5, W6, W7;

  not not_1 (not_1_out, EVALUATE);
  Adder adder_1 (.a(IN), .b(register_1_q), .out(adder_1_out), .cin(1'b0));  // open: cout
  Register register_1 (.D(adder_1_out), .en(not_1_out), .Q(register_1_q), .clk(CLK), .clr(FUNC_CLEAR));
  // Transmission_Gate #(.gate("br"), .width(8)) transmission_1: pin names not known; wires that end beside it: register_1_q, EVALUATE, not_1_out, transmission_1_p4
  Transistor #(.\type ("n"), .width(8)) transistor_1 (.in({8{1'b0}}), .out(transmission_1_p4), .gate(not_1_out));
  _8WeightBank u_8weightbank_1 (
    .W_WRITE(W_WRITE), .W_SLCT(W_SLCT), .W_IN(W_IN), .CLEAR(CLEAR), .W0(W0), .W1(W1), .W2(W2), .W3(W3),
    .W4(W4), .W5(W5), .W6(W6), .W7(W7));
  Adder adder_2 (.a(transmission_1_p4), .b(BIAS), .out(FUNC_OUT), .cin(1'b0));  // open: cout
  Multiplier multiplier_1 (.a(FUNC_OUT), .b(W0), .out(multiplier_1_out), .cin({8{1'b0}}));  // open: cout
  Multiplier multiplier_2 (.a(FUNC_OUT), .b(W1), .out(multiplier_2_out), .cin({8{1'b0}}));  // open: cout
  Multiplier multiplier_3 (.a(FUNC_OUT), .b(W2), .out(multiplier_3_out), .cin({8{1'b0}}));  // open: cout
  Multiplier multiplier_4 (.a(FUNC_OUT), .b(W3), .out(multiplier_4_out), .cin({8{1'b0}}));  // open: cout
  Multiplier multiplier_5 (.a(FUNC_OUT), .b(W4), .out(multiplier_5_out), .cin({8{1'b0}}));  // open: cout
  Multiplier multiplier_6 (.a(FUNC_OUT), .b(W5), .out(multiplier_6_out), .cin({8{1'b0}}));  // open: cout
  Multiplier multiplier_7 (.a(FUNC_OUT), .b(W6), .out(multiplier_7_out), .cin({8{1'b0}}));  // open: cout
  Multiplier multiplier_8 (.a(FUNC_OUT), .b(W7), .out(multiplier_8_out), .cin({8{1'b0}}));  // open: cout
  Register #(.trigger("high")) register_2 (.D(multiplier_1_out), .en(1'b1), .Q(E0), .clk(EVALUATE), .clr(CLEAR));
  Register #(.trigger("high")) register_3 (.D(multiplier_2_out), .en(1'b1), .Q(E1), .clk(EVALUATE), .clr(CLEAR));
  Register #(.trigger("high")) register_4 (.D(multiplier_3_out), .en(1'b1), .Q(E2), .clk(EVALUATE), .clr(CLEAR));
  Register #(.trigger("high")) register_5 (.D(multiplier_4_out), .en(1'b1), .Q(E3), .clk(EVALUATE), .clr(CLEAR));
  Register #(.trigger("high")) register_6 (.D(multiplier_5_out), .en(1'b1), .Q(E4), .clk(EVALUATE), .clr(CLEAR));
  Register #(.trigger("high")) register_7 (.D(multiplier_6_out), .en(1'b1), .Q(E5), .clk(EVALUATE), .clr(CLEAR));
  Register #(.trigger("high")) register_8 (.D(multiplier_7_out), .en(1'b1), .Q(E6), .clk(EVALUATE), .clr(CLEAR));
  Register #(.trigger("high")) register_9 (.D(multiplier_8_out), .en(1'b1), .Q(E7), .clk(EVALUATE), .clr(CLEAR));

  // Other names for the same wires on the sheet: E0_OUT[7:0] = E0; E1_OUT[7:0] = E1; E2_OUT[7:0] = E2;
  //   E3_OUT[7:0] = E3; E4_OUT[7:0] = E4; E5_OUT[7:0] = E5; E6_OUT[7:0] = E6; E7_OUT[7:0] = E7;
  //   W_SELECT[2:0] = W_SLCT

  // Notes on the sheet:
  //   Linear Addition
  //   Weight Writing/Storage
  //   Weight Multiplication
  //   Input
  //   Output
endmodule

module WeightStorage (
  output [7:0] W0,
  output [7:0] W1,
  output [7:0] W2,
  output [7:0] W3,
  output [7:0] W4,
  output [7:0] W5,
  output [7:0] W6,
  output [7:0] W7
);

  wire _0Write, _1Write, _2Write, _3Write, _4Write, _5Write, _6Write, _7Write, CLEAR;
  wire [2:0] RD_SLCT, SLCT, W_SLCT;
  wire [7:0] _0W0, _0W1, _0W2, _0W3, _0W4, _0W5, _0W6, _0W7, _1W0, _1W1, _1W2, _1W3, _1W4, _1W5, _1W6, _1W7,
       _2W0, _2W1, _2W2, _2W3, _2W4, _2W5, _2W6, _2W7, _3W0, _3W1, _3W2, _3W3, _3W4, _3W5, _3W6, _3W7, _4W0,
       _4W1, _4W2, _4W3, _4W4, _4W5, _4W6, _4W7, _5W0, _5W1, _5W2, _5W3, _5W4, _5W5, _5W6, _5W7, _6W0, _6W1,
       _6W2, _6W3, _6W4, _6W5, _6W6, _6W7, _7W0, _7W1, _7W2, _7W3, _7W4, _7W5, _7W6, _7W7, W_IN;

  Decoder #(.select(3), .disabled(0), .enable("false")) decoder_1 (
    .out0(_0Write), .out1(_1Write), .out2(_2Write), .out3(_3Write), .out4(_4Write), .out5(_5Write),
    .out6(_6Write), .out7(_7Write), .sel(W_SLCT));
  _8WeightBank u_8weightbank_1 (
    .W_WRITE(_0Write), .W_SLCT(SLCT), .W_IN(W_IN), .CLEAR(CLEAR), .W0(_0W0), .W1(_0W1), .W2(_0W2), .W3(_0W3),
    .W4(_0W4), .W5(_0W5), .W6(_0W6), .W7(_0W7));
  Multiplexer #(.select(3), .width(8), .disabled(0), .enable("false")) multiplexer_1 (
    .in0(_0W0), .in1(_1W0), .in2(_2W0), .in3(_3W0), .in4(_4W0), .in5(_5W0), .in6(_6W0), .in7(_7W0), .out(W0),
    .sel(RD_SLCT));
  _8WeightBank u_8weightbank_2 (
    .W_WRITE(_1Write), .W_SLCT(SLCT), .W_IN(W_IN), .CLEAR(CLEAR), .W0(_1W0), .W1(_1W1), .W2(_1W2), .W3(_1W3),
    .W4(_1W4), .W5(_1W5), .W6(_1W6), .W7(_1W7));
  Multiplexer #(.select(3), .width(8), .disabled(0), .enable("false")) multiplexer_2 (
    .in0(_0W1), .in1(_1W1), .in2(_2W1), .in3(_3W1), .in4(_4W1), .in5(_5W1), .in6(_6W1), .in7(_7W1), .out(W1),
    .sel(RD_SLCT));
  _8WeightBank u_8weightbank_3 (
    .W_WRITE(_2Write), .W_SLCT(SLCT), .W_IN(W_IN), .CLEAR(CLEAR), .W0(_2W0), .W1(_2W1), .W2(_2W2), .W3(_2W3),
    .W4(_2W4), .W5(_2W5), .W6(_2W6), .W7(_2W7));
  Multiplexer #(.select(3), .width(8), .disabled(0), .enable("false")) multiplexer_3 (
    .in0(_0W2), .in1(_1W2), .in2(_2W2), .in3(_3W2), .in4(_4W2), .in5(_5W2), .in6(_6W2), .in7(_7W2), .out(W2),
    .sel(RD_SLCT));
  _8WeightBank u_8weightbank_4 (
    .W_WRITE(_3Write), .W_SLCT(SLCT), .W_IN(W_IN), .CLEAR(CLEAR), .W0(_3W0), .W1(_3W1), .W2(_3W2), .W3(_3W3),
    .W4(_3W4), .W5(_3W5), .W6(_3W6), .W7(_3W7));
  Multiplexer #(.select(3), .width(8), .disabled(0), .enable("false")) multiplexer_4 (
    .in0(_0W3), .in1(_1W3), .in2(_2W3), .in3(_3W3), .in4(_4W3), .in5(_5W3), .in6(_6W3), .in7(_7W3), .out(W3),
    .sel(RD_SLCT));
  _8WeightBank u_8weightbank_5 (
    .W_WRITE(_4Write), .W_SLCT(SLCT), .W_IN(W_IN), .CLEAR(CLEAR), .W0(_4W0), .W1(_4W1), .W2(_4W2), .W3(_4W3),
    .W4(_4W4), .W5(_4W5), .W6(_4W6), .W7(_4W7));
  Multiplexer #(.select(3), .width(8), .disabled(0), .enable("false")) multiplexer_5 (
    .in0(_0W4), .in1(_1W4), .in2(_2W4), .in3(_3W4), .in4(_4W4), .in5(_5W4), .in6(_6W4), .in7(_7W4), .out(W4),
    .sel(RD_SLCT));
  _8WeightBank u_8weightbank_6 (
    .W_WRITE(_5Write), .W_SLCT(SLCT), .W_IN(W_IN), .CLEAR(CLEAR), .W0(_5W0), .W1(_5W1), .W2(_5W2), .W3(_5W3),
    .W4(_5W4), .W5(_5W5), .W6(_5W6), .W7(_5W7));
  _8WeightBank u_8weightbank_7 (
    .W_WRITE(_6Write), .W_SLCT(SLCT), .W_IN(W_IN), .CLEAR(CLEAR), .W0(_6W0), .W1(_6W1), .W2(_6W2), .W3(_6W3),
    .W4(_6W4), .W5(_6W5), .W6(_6W6), .W7(_6W7));
  Multiplexer #(.select(3), .width(8), .disabled(0), .enable("false")) multiplexer_6 (
    .in0(_0W5), .in1(_1W5), .in2(_2W5), .in3(_3W5), .in4(_4W5), .in5(_5W5), .in6(_6W5), .in7(_7W5), .out(W5),
    .sel(RD_SLCT));
  _8WeightBank u_8weightbank_8 (
    .W_WRITE(_7Write), .W_SLCT(SLCT), .W_IN(W_IN), .CLEAR(CLEAR), .W0(_7W0), .W1(_7W1), .W2(_7W2), .W3(_7W3),
    .W4(_7W4), .W5(_7W5), .W6(_7W6), .W7(_7W7));
  Multiplexer #(.select(3), .width(8), .disabled(0), .enable("false")) multiplexer_7 (
    .in0(_0W6), .in1(_1W6), .in2(_2W6), .in3(_3W6), .in4(_4W6), .in5(_5W6), .in6(_6W6), .in7(_7W6), .out(W6),
    .sel(RD_SLCT));
  Multiplexer #(.select(3), .width(8), .disabled(0), .enable("false")) multiplexer_8 (
    .in0(_0W7), .in1(_1W7), .in2(_2W7), .in3(_3W7), .in4(_4W7), .in5(_5W7), .in6(_6W7), .in7(_7W7), .out(W7),
    .sel(RD_SLCT));

  // Other names for the same wires on the sheet: OUT_W0[7:0] = W0; OUT_W1[7:0] = W1; OUT_W2[7:0] = W2;
  //   OUT_W3[7:0] = W3; OUT_W4[7:0] = W4; OUT_W5[7:0] = W5; OUT_W6[7:0] = W6; OUT_W7[7:0] = W7

  // Notes on the sheet:
  //   NODE 0
  //   Weight Storage Banks
  //   NODE 1
  //   Node Read Selection
  //   NODE 2
  //   NODE 3
  //   NODE 4
  //   NODE 5
  //   NODE 6
  //   NODE 7
endmodule

module _8WeightBank (
  input  W_WRITE,
  input  [2:0] W_SLCT,
  input  [7:0] W_IN,
  input  CLEAR,
  output [7:0] W0,
  output [7:0] W1,
  output [7:0] W2,
  output [7:0] W3,
  output [7:0] W4,
  output [7:0] W5,
  output [7:0] W6,
  output [7:0] W7
);

  wire decoder_1_out0, decoder_1_out1, decoder_1_out2, decoder_1_out3, decoder_1_out4, decoder_1_out5,
       decoder_1_out6, decoder_1_out7, W0_Write, W1_Write, W2_Write, W3_Write, W4_Write, W5_Write, W6_Write,
       W7_Write;

  Decoder #(.select(3), .disabled(0), .enable("false")) decoder_1 (
    .out0(decoder_1_out0), .out1(decoder_1_out1), .out2(decoder_1_out2), .out3(decoder_1_out3),
    .out4(decoder_1_out4), .out5(decoder_1_out5), .out6(decoder_1_out6), .out7(decoder_1_out7), .sel(W_SLCT));
  and and_1 (W0_Write, decoder_1_out0, W_WRITE);
  and and_2 (W1_Write, decoder_1_out1, W_WRITE);
  and and_3 (W2_Write, decoder_1_out2, W_WRITE);
  and and_4 (W3_Write, decoder_1_out3, W_WRITE);
  and and_5 (W4_Write, decoder_1_out4, W_WRITE);
  and and_6 (W5_Write, decoder_1_out5, W_WRITE);
  and and_7 (W6_Write, decoder_1_out6, W_WRITE);
  and and_8 (W7_Write, decoder_1_out7, W_WRITE);
  Register #(.trigger("high")) register_1 (.D(W_IN), .en(1'b1), .Q(W0), .clk(W0_Write), .clr(CLEAR));
  Register #(.trigger("high")) register_2 (.D(W_IN), .en(1'b1), .Q(W1), .clk(W1_Write), .clr(CLEAR));
  Register #(.trigger("high")) register_3 (.D(W_IN), .en(1'b1), .Q(W2), .clk(W2_Write), .clr(CLEAR));
  Register #(.trigger("high")) register_4 (.D(W_IN), .en(1'b1), .Q(W3), .clk(W3_Write), .clr(CLEAR));
  Register #(.trigger("high")) register_5 (.D(W_IN), .en(1'b1), .Q(W4), .clk(W4_Write), .clr(CLEAR));
  Register #(.trigger("high")) register_6 (.D(W_IN), .en(1'b1), .Q(W5), .clk(W5_Write), .clr(CLEAR));
  Register #(.trigger("high")) register_7 (.D(W_IN), .en(1'b1), .Q(W6), .clk(W6_Write), .clr(CLEAR));
  Register #(.trigger("high")) register_8 (.D(W_IN), .en(1'b1), .Q(W7), .clk(W7_Write), .clr(CLEAR));

  // Other names for the same wires on the sheet: W_SELECT[2:0] = W_SLCT

  // Notes on the sheet:
  //   Weight Writing/Storage
  //   Input
  //   Output
endmodule
